// Logisim project lab2.circ as structural Verilog: 1 circuit, main circuit main
module main (
);

  wire nand_1_out, nand_2_out, nand_3_out, nand_4_out, nand_5_out, nand_6_out, nand_7_out, nand_8_out,
       nand_9_out, nand_10_out, nand_11_out, nand_12_out, nand_13_out, nand_14_out, nand_15_out, nand_16_out,
       nand_17_out, nand_18_out, nand_19_out, nand_20_out, nor_1_out, nor_2_out, undriven, undriven_2,
       undriven_3, undriven_4, undriven_5, undriven_6, undriven_7, undriven_8, undriven_9, undriven_10,
       undriven_11, undriven_12, undriven_13;

  nand nand_1 (nand_1_out, undriven, undriven_3);
  nand nand_2 (nand_2_out, undriven_3, undriven_2);
  nor nor_1 (nor_1_out, undriven_6, nor_2_out);
  nor nor_2 (nor_2_out, nor_1_out, undriven_7);
  nand nand_3 (nand_3_out, undriven_4, nand_4_out);
  nand nand_4 (nand_4_out, nand_3_out, undriven_5);
  nand nand_5 (nand_5_out, nand_1_out, nand_6_out);
  nand nand_6 (nand_6_out, nand_5_out, nand_2_out);
  nand nand_7 (nand_7_out, undriven_8, undriven_8);
  nand nand_8 (nand_8_out, nand_7_out, undriven_9);
  nand nand_9 (nand_9_out, undriven_10, nand_10_out);
  nand nand_10 (nand_10_out, undriven_13, undriven_13);
  nand nand_11 (nand_11_out, undriven_12, undriven_12);
  nand nand_12 (nand_12_out, undriven_11, undriven_11);
  nand nand_13 (nand_13_out, undriven_12, nand_12_out);
  nand nand_14 (nand_14_out, nand_11_out, undriven_11);
  nand nand_15 (nand_15_out, nand_7_out, nand_16_out);
  nand nand_16 (nand_16_out, nand_15_out, nand_8_out);
  nand nand_17 (nand_17_out, nand_9_out, nand_18_out);
  nand nand_18 (nand_18_out, nand_17_out, nand_10_out);
  nand nand_19 (nand_19_out, nand_13_out, nand_20_out);
  nand nand_20 (nand_20_out, nand_19_out, nand_14_out);

  // Notes on the sheet:
  //   S
  //   R
  //   S
  //   C
  //   R
  //   R
  //   S
  //   Асинхронный RS триггер с прямыми входами (2 элемента ИЛИ-НЕ)
  //   Асинхронный RS триггер с инверсными входами (2 элемента И-НЕ)
  //   Синхронный RS триггер
  //   Q
  //   !Q
  //   Q
  //   !Q
  //   Q
  //   !Q
  //   S
  //   R
  //   S
  //   R
  //   S
  //   R
  //   Модификации RS тригера
  //   S-тригер
  //   R-тригер
  //   E-тригер
  //   Q
  //   !Q
  //   Q
  //   !Q
  //   Q
  //   !Q
endmodule
